# Fritzing sketch YunSensorMote (saved by Fritzing 0.9.3b)

parts:
  Sunfounder2 = Analog Temeprature Sensor [package=THT]
  Componente1 = Arduino Yun
  Sunfounder1 = Humidity Sensor DHT11 [package=THT]
  U1 = POT [package=pot_mammoth]
  Sunfounder4 = Relay module [package=THT]
  Componente2 = MPL3115A2 I2C Barometric Pressure, Altitude, Temperature Sensor
  Sunfounder5 = Analog LDR Sensor [package=THT]

nets:
  GND: Sunfounder2.GND, Componente1.GND, Sunfounder1.GND, Sunfounder4.GND, Componente2.GND
  VCC: Sunfounder2.Vcc, Componente1.5V, Sunfounder1.Vcc, U1.S, Sunfounder4.Vcc
  N1: Sunfounder2.Vout, Componente1.A0
  N2: Componente1.A1, Sunfounder1.Vout
  N3: Componente1.A2, Sunfounder5.Vout
  N4: Componente1.A3, U1.A
  N5: Componente1.D8, Sunfounder4.Vout
  N6: Componente1.D2, Componente2.SDA
  N7: Componente1.D3_PWM, Componente2.SCL
  3V3: Componente1.3V3, Componente2.VIN

notes:
  Temperature Sensor
  Humidity Sensor
  Simulate any analog Sensor
  Relay Module
  Barometric MPL3115A2
  LDR Sensor

custom parts:
  Analog Temeprature Sensor: Analog Temeprature Sensor with thermistor for Sunfounder 37 Sensor Kit
  Humidity Sensor DHT11: Humidity Sensor DHT11 for Sunfounder 37 Sensor Kit
  Relay module: Relay Module for Sunfounder 37 Sensor Kit
  MPL3115A2 I2C Barometric Pressure, Altitude, Temperature Sensor: This pressure sensor from Freescale is a great low-cost sensing solution for precision measurement of barometric pressure and altitude. The MPL3115A2 has a typical 1.5 Pascal resolution, which can resolve altitude at 0.3 meters (compare to the BMP180 which can do 0.17m). It has some upsides compared to the BMP180, such as interrupt outputs for ultra-low power usage, and its also a heck of a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
  Analog LDR Sensor: Analog Photoresistor Sensor for Sunfounder 37 Sensor Kit
